// Logisim project CS23B1097_LAB5.circ as structural Verilog: 2 circuits, main circuit main
module main (
  input  X0,
  input  Y0,
  input  C0,
  input  X1,
  input  Y1,
  input  in_6,
  input  X2,
  input  Y2,
  input  X3,
  input  Y3
);

  wire and_1_out, and_2_out, and_3_out, and_4_out, and_5_out, and_6_out, and_7_out, and_8_out, and_9_out,
       and_10_out, fulladder_1_g0, fulladder_1_p0, fulladder_2_g0, fulladder_2_p0, fulladder_3_g0,
       fulladder_3_p0, fulladder_4_g0, fulladder_4_p0, or_1_out, or_2_out, or_3_out;
  wire [0:0] or_4_out;
  wire [3:0] fulladder_1_s;

  FULLADDER fulladder_1 (.X(X0), .Y(Y0), .C0(C0), .P0(fulladder_1_p0), .S(fulladder_1_s[0]), .G0(fulladder_1_g0));
  FULLADDER fulladder_2 (.X(X1), .Y(Y1), .C0(or_1_out), .P0(fulladder_2_p0), .S(fulladder_1_s[1]), .G0(fulladder_2_g0));
  FULLADDER fulladder_3 (.X(X2), .Y(Y2), .C0(or_2_out), .P0(fulladder_3_p0), .S(fulladder_1_s[2]), .G0(fulladder_3_g0));
  FULLADDER fulladder_4 (.X(X3), .Y(Y3), .C0(or_3_out), .P0(fulladder_4_p0), .S(fulladder_1_s[3]), .G0(fulladder_4_g0));
  and and_1 (and_1_out, C0, fulladder_1_p0);
  and and_2 (and_2_out, fulladder_1_g0, fulladder_2_p0);
  and and_3 (and_3_out, fulladder_4_p0, fulladder_3_p0, fulladder_2_g0);
  and and_4 (and_4_out, fulladder_2_p0, fulladder_3_p0, fulladder_4_p0, fulladder_1_g0);
  and and_5 (and_5_out, fulladder_1_p0, fulladder_2_p0, fulladder_3_p0, fulladder_4_p0, C0);
  and and_6 (and_6_out, fulladder_2_p0, C0, fulladder_1_p0);
  and and_7 (and_7_out, fulladder_2_g0, fulladder_3_p0);
  and and_8 (and_8_out, fulladder_2_p0, fulladder_3_p0, fulladder_1_g0);
  and and_9 (and_9_out, fulladder_1_p0, fulladder_2_p0, fulladder_3_p0, C0);
  and and_10 (and_10_out, fulladder_3_g0, fulladder_4_p0);
  or or_1 (or_1_out, and_1_out, fulladder_1_g0);
  or or_2 (or_2_out, and_2_out, and_6_out, fulladder_2_g0);
  or or_3 (or_3_out, and_7_out, and_8_out, and_9_out, fulladder_3_g0);
  or or_4 (or_4_out[0], and_10_out, and_3_out, and_4_out, and_5_out, fulladder_4_g0);
  Hex_Digit_Display hex_digit_display_1 (.value({{3{in_6}}, or_4_out[0]}));  // open: dp
  Hex_Digit_Display hex_digit_display_2 (.value(fulladder_1_s));  // open: dp

  // Notes on the sheet:
  //   C1
  //   C2
  //   C3
  //   C4
endmodule

module FULLADDER (
  input  X,
  input  Y,
  input  C0,
  output P0,
  output S,
  output G0
);

  xor xor_1 (P0, X, Y);
  and and_1 (G0, X, Y);
  xor xor_2 (S, P0, C0);
endmodule
