// Logisim project CS23B1097_Labwork.circ as structural Verilog: 1 circuit, main circuit main
module main (
  input  in_1,
  input  in_2,
  input  in_3,
  input  in_4,
  input  D,
  input  [1:0] Selector,
  input  in_7,
  input  in_8,
  output Q,
  output out_10,
  output out_11,
  output out_12,
  output out_13
);

  wire clock_1_out, multiplexer_1_out, multiplexer_2_out, multiplexer_3_out, multiplexer_4_out;

  Clock clock_1 (.out(clock_1_out));
  Multiplexer #(.select(2)) multiplexer_1 (
    .in0(D), .in1(out_12), .in2(in_1), .in3(out_11), .out(multiplexer_1_out), .sel(Selector));
  D_Flip_Flop d_ff_1 (.D(multiplexer_1_out), .clk(clock_1_out), .Q(out_11), .preset(in_7), .reset(in_8));  // open: Qn
  Multiplexer #(.select(2)) multiplexer_2 (
    .in0(out_11), .in1(multiplexer_3_out), .in2(in_2), .in3(out_12), .out(multiplexer_2_out), .sel(Selector));
  D_Flip_Flop d_ff_2 (.D(multiplexer_2_out), .clk(clock_1_out), .Q(out_12), .preset(in_7), .reset(in_8));  // open: Qn
  Multiplexer #(.select(2)) multiplexer_3 (
    .in0(out_12), .in1(out_10), .in2(in_3), .in3(out_13), .out(multiplexer_3_out), .sel(Selector));
  D_Flip_Flop d_ff_3 (.D(multiplexer_3_out), .clk(clock_1_out), .Q(out_13), .preset(in_7), .reset(in_8));  // open: Qn
  D_Flip_Flop d_ff_4 (.D(multiplexer_4_out), .clk(clock_1_out), .Q(out_10), .preset(in_7), .reset(in_8));  // open: Qn
  Multiplexer #(.select(2)) multiplexer_4 (
    .in0(out_13), .in1(D), .in2(in_4), .in3(out_10), .out(multiplexer_4_out), .sel(Selector));

  assign Q = out_10;

  // Notes on the sheet:
  //   I0
  //   I1
  //   I2
  //   D
  //   I3
endmodule
